# Fritzing sketch Esp8266_Mpu6560_U8G2 (saved by Fritzing 0.8.7b)
breadboards: 1

parts:
  WeMos_D1_Mini2 = WeMos D1 Mini
  S1 = Toggle Switch [package=THT]
  Squix1 = OLED 0.96" 128x64 I2C SSD1306
  VCC1 = Battery
  元件1 = InvenSense MPU6050

nets:
  VCC: WeMos_D1_Mini2.5V, S1.COM, S1.L2, Squix1.VCC, VCC1.+, 元件1.VCC
  N1: WeMos_D1_Mini2.D2, Squix1.SCA
  N2: WeMos_D1_Mini2.D3, 元件1.SCL
  N3: WeMos_D1_Mini2.D4, 元件1.SDA
  N4: WeMos_D1_Mini2.D5, Squix1.SCL
  GND: WeMos_D1_Mini2.G, Squix1.GND, VCC1.-, 元件1.GND

custom parts:
  WeMos D1 Mini: The D1 mini is a mini wifi board based on ESP-8266EX.
